// Logisim project BPU.circ as structural Verilog
module main (
  input  [7:0] Address_bus,
  input  D__RAM,
  input  RAM__D,
  input  [7:0] Data_bus,
  input  Output_flag,
  input  [31:0] in_6
);

  wire clock_1_out, clock_2_out, clr_out, display_driver_1_ready, n0_flag_1_is_zero, Reset_out;
  wire [3:0] display_driver_1_high_nibble, display_driver_1_low_nibble;
  wire [7:0] controlled_buffer_1_out, ram_1_data;

  Clock clock_1 (.out(clock_1_out));
  Hex_Digit_Display hex_digit_display_1 (.value(display_driver_1_high_nibble));  // open: dp
  Hex_Digit_Display hex_digit_display_2 (.value(display_driver_1_low_nibble));  // open: dp
  Clock clock_2 (.out(clock_2_out));
  Button Reset (.out(Reset_out));
  RAM #(.bus("separate")) ram_1 (
    .addr(Address_bus), .din(controlled_buffer_1_out), .data(ram_1_data), .str(D__RAM), .sel(1'b1),
    .clk(clock_1_out), .ld(1'b1), .clr(clr_out));
  Button clr (.out(clr_out));
  // Probe on display_driver_1_ready
  Display_driver display_driver_1 (
    .Data_in(Data_bus), .Reset(Reset_out), .Clock(clock_2_out), .Enable(Output_flag),
    .Ready(display_driver_1_ready), .High_nibble(display_driver_1_high_nibble),
    .Low_nibble(display_driver_1_low_nibble));
  // Probe on controlled_buffer_1_out
  assign controlled_buffer_1_out = RAM__D ? ram_1_data : 8'bz;  // Controlled_Buffer controlled_buffer_1
  _0_Flag u_0_flag_1 (.Data(ram_1_data), .Is_zero(n0_flag_1_is_zero));
  // Probe on n0_flag_1_is_zero
  DotMatrix #(.matrixcols(32), .matrixrows(32)) dotmatrix_1 (.col3(in_6));  // open: col0, col1, col2, col4, col5, col6, col7, col8, col9, col10, col11, col12, col13, col14, col15, col16, col17, col18, col19, col20, col21, col22, col23, col24, col25, col26, col27, col28, col29, col30, col31
endmodule

module _0_Flag (
  input  [7:0] Data,
  output Is_zero
);

  nor nor_1 (Is_zero, Data[0], Data[1], Data[2], Data[3], Data[5], Data[6], Data[7], Data[4]);
endmodule

module BPU (
  input  Clock,
  input  Halt,
  input  Resume,
  input  Wait,
  output BPU_clock
);

  wire OR_out;

  or OR (OR_out, Resume, Wait);
  and AND (BPU_clock, Clock, Halt, OR_out);
endmodule

module Display_driver (
  input  [7:0] Data_in,
  input  Reset,
  input  Clock,
  input  Enable,
  output [3:0] High_nibble,
  output [3:0] Low_nibble,
  output Ready
);

  wire not_1_out;

  not not_1 (not_1_out, Enable);
  Register register_1 (.D(Data_in), .en(Enable), .Q({High_nibble, Low_nibble}), .clk(Clock), .clr(Reset));
  D_Flip_Flop d_ff_1 (.clk(Clock), .D(Enable), .Q(Ready), .preset(1'b0), .en(1'b1), .reset(not_1_out));  // open: Qn
endmodule

module RAM_showcase (
  input  [7:0] Address_bus,
  input  MEM__D,
  input  D__MEM
);

  wire clock_1_out, n0_flag_1_is_zero, Reset_out;
  wire [7:0] controlled_buffer_1_out, ram_1_data;

  Clock clock_1 (.out(clock_1_out));
  RAM #(.bus("separate")) ram_1 (
    .addr(Address_bus), .din(controlled_buffer_1_out), .data(ram_1_data), .str(D__MEM), .sel(1'b1),
    .clk(clock_1_out), .ld(1'b1), .clr(Reset_out));
  Button Reset (.out(Reset_out));
  assign controlled_buffer_1_out = MEM__D ? ram_1_data : 8'bz;  // Controlled_Buffer controlled_buffer_1
  // Probe on controlled_buffer_1_out
  // Probe on n0_flag_1_is_zero
  _0_Flag u_0_flag_1 (.Data(ram_1_data), .Is_zero(n0_flag_1_is_zero));
endmodule

module Output_showcase (
  input  [7:0] Data_bus,
  input  Output_flag
);

  wire clock_1_out, display_driver_1_ready, Reset_out;
  wire [3:0] display_driver_1_high_nibble, display_driver_1_low_nibble;

  Hex_Digit_Display hex_digit_display_1 (.value(display_driver_1_high_nibble));  // open: dp
  Clock clock_1 (.out(clock_1_out));
  Hex_Digit_Display hex_digit_display_2 (.value(display_driver_1_low_nibble));  // open: dp
  Display_driver display_driver_1 (
    .Data_in(Data_bus), .Reset(Reset_out), .Clock(clock_1_out), .Enable(Output_flag),
    .Ready(display_driver_1_ready), .High_nibble(display_driver_1_high_nibble),
    .Low_nibble(display_driver_1_low_nibble));
  Button Reset (.out(Reset_out));
  // Probe on display_driver_1_ready
endmodule

module Simple_showcases (
  input  in,
  input  [7:0] Address_bus,
  input  [7:0] Input,
  input  Load_RAM_from_ROM,
  input  Clock,
  input  Halt,
  input  Resume,
  input  Wait,
  output BPU_clock
);

  wire Confirm_out, OR_out;
  wire [7:0] controlled_buffer_1_out, rom_1_data;

  or OR (OR_out, Resume, Wait);
  ROM rom_1 (.addr(Address_bus), .data(rom_1_data), .sel(Load_RAM_from_ROM));
  // Probe on rom_1_data
  // Probe on Load_RAM_from_ROM
  and AND (BPU_clock, Clock, Halt, OR_out);
  LED Input_request (.in(in));
  assign controlled_buffer_1_out = in ? Input : 8'bz;  // Controlled_Buffer controlled_buffer_1
  Button Confirm (.out(Confirm_out));
  // Probe on controlled_buffer_1_out
  // Probe on Confirm_out

  // Notes on the sheet:
  //   ROM
  //   Clock logic
  //   Input
endmodule

module Register_showcases (
  input  D__DP,
  input  [7:0] Data_bus,
  input  DP__D,
  input  D__PR,
  input  DP__A,
  input  NEG,
  input  _0,
  input  D__PC,
  input  PC_plus_plus,
  input  PC__D,
  input  PC__A
);

  wire AND_out, clock_1_out, clock_2_out, clock_3_out, Reset_2_out, Reset_out, XOR_out;
  wire [7:0] controlled_buffer_1_out, controlled_buffer_2_out, controlled_buffer_3_out,
       controlled_buffer_4_out, counter_1_q, register_1_q, register_2_q;

  assign controlled_buffer_1_out = DP__A ? register_1_q : 8'bz;  // Controlled_Buffer controlled_buffer_1
  // Probe on controlled_buffer_1_out
  Register register_1 (.D(controlled_buffer_2_out), .en(D__DP), .Q(register_1_q), .clk(clock_1_out), .clr(Reset_out));
  Button Reset (.out(Reset_out));
  Clock clock_1 (.out(clock_1_out));
  xor XOR (XOR_out, NEG, _0);
  // Probe on controlled_buffer_3_out
  assign controlled_buffer_2_out = DP__D ? register_1_q : 8'bz;  // Controlled_Buffer controlled_buffer_2
  // Probe on controlled_buffer_2_out
  and AND (AND_out, XOR_out, D__PC);
  assign controlled_buffer_3_out = PC__A ? counter_1_q : 8'bz;  // Controlled_Buffer controlled_buffer_3
  Clock clock_2 (.out(clock_2_out));
  // Probe on controlled_buffer_4_out
  Counter counter_1 (
    .load(AND_out), .D(controlled_buffer_4_out), .count(PC_plus_plus), .Q(counter_1_q), .clk(clock_2_out),
    .clr(Reset_2_out));  // open: carry
  assign controlled_buffer_4_out = PC__D ? counter_1_q : 8'bz;  // Controlled_Buffer controlled_buffer_4
  Button Reset_2 (.out(Reset_2_out));
  Clock clock_3 (.out(clock_3_out));
  // Probe on register_2_q[7:3]
  Register register_2 (.D(Data_bus), .en(D__PR), .Q(register_2_q), .clk(clock_3_out));  // open: clr
  // Probe on register_2_q[0]
  // Probe on register_2_q[2:0]

  // Notes on the sheet:
  //   Data pointer
  //   Program counter
  //   Program register
endmodule
